// Logisim project Somador4bits.circ as structural Verilog: 4 circuits, main circuit main
module main (
  input  Ci,
  input  A0,
  input  A1,
  input  A2,
  input  A3,
  input  B0,
  input  B1,
  input  B2,
  input  B3,
  output s0,
  output s1,
  output s2,
  output s3,
  output Co
);

  Somador_de_4_bits somador_de_4_bits_1 (
    .x0(A0), .x1(A1), .x2(A2), .x3(A3), .y0(B0), .y1(B1), .y2(B2), .y3(B3), .ci(Ci), .Co(Co), .s0(s0),
    .s1(s1), .s2(s2), .s3(s3));
endmodule

module MeioSomador (
  input  x0,
  input  y0,
  output s0,
  output Co0
);

  and and_1 (Co0, y0, x0);
  xor xor_1 (s0, x0, y0);
endmodule

module SomadorCompleto (
  input  Ci1,
  input  x1,
  input  y1,
  output s1,
  output Co1
);

  wire meiosomador_1_co0, meiosomador_1_s0, meiosomador_2_co0;

  MeioSomador meiosomador_1 (.x0(x1), .y0(y1), .Co0(meiosomador_1_co0), .s0(meiosomador_1_s0));
  or or_1 (Co1, meiosomador_1_co0, meiosomador_2_co0);
  MeioSomador meiosomador_2 (.x0(Ci1), .y0(meiosomador_1_s0), .Co0(meiosomador_2_co0), .s0(s1));
endmodule

module Somador_de_4_bits (
  input  ci,
  input  x0,
  input  x1,
  input  x2,
  input  x3,
  input  y0,
  input  y1,
  input  y2,
  input  y3,
  output s0,
  output s1,
  output s2,
  output s3,
  output Co
);

  wire somadorcompleto_1_co1, somadorcompleto_2_co1, somadorcompleto_3_co1;

  SomadorCompleto somadorcompleto_1 (.x1(x0), .y1(x1), .Ci1(ci), .Co1(somadorcompleto_1_co1), .s1(s0));
  SomadorCompleto somadorcompleto_2 (
    .x1(x2), .y1(x3), .Ci1(somadorcompleto_1_co1), .Co1(somadorcompleto_2_co1), .s1(s1));
  SomadorCompleto somadorcompleto_3 (
    .x1(y0), .y1(y1), .Ci1(somadorcompleto_2_co1), .Co1(somadorcompleto_3_co1), .s1(s2));
  SomadorCompleto somadorcompleto_4 (.x1(y2), .y1(y3), .Ci1(somadorcompleto_3_co1), .Co1(Co), .s1(s3));
endmodule
